// Logisim project Decoder y Display.circ as structural Verilog: 3 circuits, main circuit main
module main (
  input  [31:0] in_1
);

  wire [2:0] funct3;
  wire [4:0] Rd, rs1, rs2;
  wire [6:0] Display_displayfunct3, Display_displayfunct7, Display_displayop, Display_displayrd,
       Display_displayrs1, Display_displayrs2, funct7, OP;

  Decoder Decoder (.in_1(in_1), .Opcode(OP), .Rd(Rd), .Funct3(funct3), .Rs1(rs1), .Rs2(rs2), .Funct7(funct7));
  Display Display (
    .Opcode(OP), .Rd(Rd), .funct3(funct3), .Rs1(rs1), .Rs2(rs2), .funct7(funct7),
    .DisplayOp(Display_displayop), .DisplayRd(Display_displayrd), .DisplayFunct3(Display_displayfunct3),
    .DisplayRs1(Display_displayrs1), .DisplayRs2(Display_displayrs2), .DisplayFunct7(Display_displayfunct7));
  _7_Segment_Display u_7_segment_display_1 (
    .g(Display_displayop[6]), .f(Display_displayop[5]), .a(Display_displayop[0]), .b(Display_displayop[1]),
    .e(Display_displayop[4]), .d(Display_displayop[3]), .c(Display_displayop[2]));  // open: dp
  _7_Segment_Display u_7_segment_display_2 (
    .g(Display_displayrd[6]), .f(Display_displayrd[5]), .a(Display_displayrd[0]), .b(Display_displayrd[1]),
    .e(Display_displayrd[4]), .d(Display_displayrd[3]), .c(Display_displayrd[2]));  // open: dp
  _7_Segment_Display u_7_segment_display_3 (
    .g(Display_displayfunct3[6]), .f(Display_displayfunct3[5]), .a(Display_displayfunct3[0]),
    .b(Display_displayfunct3[1]), .e(Display_displayfunct3[4]), .d(Display_displayfunct3[3]),
    .c(Display_displayfunct3[2]));  // open: dp
  _7_Segment_Display u_7_segment_display_4 (
    .g(Display_displayrs1[6]), .f(Display_displayrs1[5]), .a(Display_displayrs1[0]),
    .b(Display_displayrs1[1]), .e(Display_displayrs1[4]), .d(Display_displayrs1[3]), .c(Display_displayrs1[2]));  // open: dp
  _7_Segment_Display u_7_segment_display_5 (
    .g(Display_displayrs2[6]), .f(Display_displayrs2[5]), .a(Display_displayrs2[0]),
    .b(Display_displayrs2[1]), .e(Display_displayrs2[4]), .d(Display_displayrs2[3]), .c(Display_displayrs2[2]));  // open: dp
  _7_Segment_Display u_7_segment_display_6 (
    .g(Display_displayfunct7[6]), .f(Display_displayfunct7[5]), .a(Display_displayfunct7[0]),
    .b(Display_displayfunct7[1]), .e(Display_displayfunct7[4]), .d(Display_displayfunct7[3]),
    .c(Display_displayfunct7[2]));  // open: dp
endmodule

module Decoder (
  input  [31:0] in_1,
  output [6:0] Opcode,
  output [4:0] Rd,
  output [2:0] Funct3,
  output [4:0] Rs1,
  output [4:0] Rs2,
  output [6:0] Funct7
);


  assign Funct3 = in_1[14:12];
  assign Funct7 = in_1[31:25];
  assign Opcode = in_1[6:0];
  assign Rd = in_1[11:7];
  assign Rs1 = in_1[19:15];
  assign Rs2 = in_1[24:20];
endmodule

module Display (
  input  [6:0] Opcode,
  input  [4:0] Rd,
  input  [2:0] funct3,
  input  [4:0] Rs1,
  input  [4:0] Rs2,
  input  [6:0] funct7,
  output [6:0] DisplayOp,
  output [6:0] DisplayRd,
  output [6:0] DisplayFunct3,
  output [6:0] DisplayRs1,
  output [6:0] DisplayRs2,
  output [6:0] DisplayFunct7
);

  wire comparator_1_eq, comparator_2_eq, comparator_3_eq, comparator_4_eq, comparator_5_eq, comparator_6_eq;

  Comparator #(.width(7)) comparator_1 (.a(Opcode), .b({7{1'b0}}), .eq(comparator_1_eq));  // open: gt, lt
  Comparator #(.width(5)) comparator_2 (.a(Rd), .b({5{1'b0}}), .eq(comparator_2_eq));  // open: gt, lt
  Comparator #(.width(3)) comparator_3 (.a(funct3), .b(3'b000), .eq(comparator_3_eq));  // open: gt, lt
  Comparator #(.width(5)) comparator_4 (.a(Rs1), .b({5{1'b0}}), .eq(comparator_4_eq));  // open: gt, lt
  Comparator #(.width(5)) comparator_5 (.a(Rs2), .b({5{1'b0}}), .eq(comparator_5_eq));  // open: gt, lt
  assign DisplayRd = comparator_2_eq ? 7'b1110011 : 7'bz;  // Controlled_Buffer controlled_buffer_1
  assign DisplayFunct3 = comparator_3_eq ? 7'b0111001 : 7'bz;  // Controlled_Buffer controlled_buffer_2
  assign DisplayRs1 = comparator_4_eq ? 7'b0001000 : 7'bz;  // Controlled_Buffer controlled_buffer_3
  assign DisplayRs2 = comparator_5_eq ? 7'b1011011 : 7'bz;  // Controlled_Buffer controlled_buffer_4
  Comparator #(.width(7)) comparator_6 (.a(funct7), .b({7{1'b0}}), .eq(comparator_6_eq));  // open: gt, lt
  assign DisplayOp = comparator_1_eq ? 7'b0001000 : 7'bz;  // Controlled_Buffer controlled_buffer_5
  assign DisplayFunct7 = comparator_6_eq ? 7'b0001000 : 7'bz;  // Controlled_Buffer controlled_buffer_6
endmodule
